// Logisim project procesador.circ as structural Verilog: 2 circuits, main circuit main
module main (
  input  [7:0] Register_A,
  input  [7:0] Register_B,
  input  [7:0] RAM_VALUE,
  input  [7:0] PC,
  input  [7:0] Instruction
);

  wire comparator_1_eq;
  wire [7:0] adder_1_out, multiplexer_1_out, multiplexer_2_out, subtractor_1_out;

  // Probe on Instruction[2:0]
  // Probe on Instruction[7:3]
  Adder adder_1 (.a(Register_A), .b(Register_B), .out(adder_1_out));  // open: cin, cout
  Subtractor subtractor_1 (.a(Register_A), .b(Register_B), .out(subtractor_1_out));  // open: bin, bout
  Multiplexer #(.width(8)) multiplexer_1 (.in0(PC), .in1(Register_B), .out(multiplexer_1_out), .sel(comparator_1_eq));
  Comparator comparator_1 (.a(Register_A), .b({8{1'b0}}), .eq(comparator_1_eq));  // open: gt, lt
  ALU alu_1 ();  // open: Register_A, Register_B, RAM_VALUE, PC, Instruction
  Multiplexer #(.select(3), .width(8)) multiplexer_2 (
    .in0({Instruction[7:3], 3'b000}), .in1(Register_A), .in2(RAM_VALUE), .in3(adder_1_out),
    .in4(subtractor_1_out), .in5(multiplexer_1_out), .in6({8{1'b0}}), .in7({8{1'b0}}), .out(multiplexer_2_out));  // open: sel
  // Probe on multiplexer_2_out
  RAM ram_1 ();  // open: addr, we, oe, clk, din, dout

  // Notes on the sheet:
  //   ALU
endmodule

module ALU (
  input  [7:0] Register_A,
  input  [7:0] Register_B,
  input  [7:0] RAM_VALUE,
  input  [7:0] PC,
  input  [7:0] Instruction
);

  wire comparator_1_eq;
  wire [7:0] adder_1_out, multiplexer_1_out, multiplexer_2_out, subtractor_1_out;

  // Probe on Instruction[2:0]
  // Probe on Instruction[7:3]
  Adder adder_1 (.a(Register_A), .b(Register_B), .out(adder_1_out));  // open: cin, cout
  Subtractor subtractor_1 (.a(Register_A), .b(Register_B), .out(subtractor_1_out));  // open: bin, bout
  Multiplexer #(.width(8)) multiplexer_1 (.in0(PC), .in1(Register_B), .out(multiplexer_1_out), .sel(comparator_1_eq));
  Comparator comparator_1 (.a(Register_A), .b({8{1'b0}}), .eq(comparator_1_eq));  // open: gt, lt
  // Probe on multiplexer_2_out
  Multiplexer #(.select(3), .width(8)) multiplexer_2 (
    .in0({Instruction[7:3], 3'b000}), .in1(Register_A), .in2(RAM_VALUE), .in3(adder_1_out),
    .in4(subtractor_1_out), .in5(multiplexer_1_out), .in6({8{1'b0}}), .in7({8{1'b0}}), .out(multiplexer_2_out));  // open: sel

  // Notes on the sheet:
  //   ALU
endmodule
