// Logisim project procesador.circ as structural Verilog: 1 circuit, main circuit main
module main (
  input  [7:0] Register_A,
  input  [7:0] Register_B,
  input  [7:0] RAM_VALUE,
  input  [7:0] PC,
  input  [7:0] Instruction
);

  wire comparator_1_eq;
  wire [7:0] adder_1_out, multiplexer_1_out, multiplexer_2_out, subtractor_1_out, undriven;

  Clock clock_1 ();  // open: out
  Register register_1 ();  // open: D, en, clk, Q, clr
  // Probe on Instruction[2:0]
  // Probe on Instruction[7:3]
  Adder adder_1 (.a(Register_A), .b(undriven), .out(adder_1_out));  // open: cin, cout
  Subtractor subtractor_1 (.a(Register_A), .b(undriven), .out(subtractor_1_out));  // open: bin, bout
  Comparator comparator_1 (.a(Register_A), .b({8{1'b0}}), .eq(comparator_1_eq));  // open: gt, lt
  Multiplexer #(.width(8)) multiplexer_1 (.in0(PC), .in1(undriven), .out(multiplexer_1_out), .sel(comparator_1_eq));
  // Probe on multiplexer_2_out
  Multiplexer #(.select(3), .width(8)) multiplexer_2 (
    .in0({Instruction[7:3], 3'b000}), .in1(undriven), .in2(Register_A), .in3(adder_1_out),
    .in4(subtractor_1_out), .in5(undriven), .in6(multiplexer_1_out), .in7({8{1'b0}}),
    .out(multiplexer_2_out), .sel(Instruction[2:0]));
  RAM ram_1 ();  // open: addr, we, oe, clk, din, dout
endmodule
